# Fritzing sketch FunkPumpkin (saved by Fritzing 0.9.0b)
breadboards: 1

parts:
  Part1 = Arduino Uno (Rev3)
  R1 = Resistor [tolerance=±5% resistance=330 package=THT]
  R2 = Resistor [tolerance=±5% resistance=330 package=THT]
  R3 = Resistor [tolerance=±5% resistance=330 package=THT]
  R4 = Resistor [tolerance=±5% resistance=330 package=THT]
  R5 = Resistor [tolerance=±5% resistance=330 package=THT]
  R6 = Resistor [tolerance=±5% resistance=330 package=THT]
  Q1 = NPN-Transistor [part_number=2222a package="TO92 [THT]"]
  Q2 = NPN-Transistor [part_number=2222a package="TO92 [THT]"]
  Q3 = NPN-Transistor [part_number=2222a package="TO92 [THT]"]
  Q4 = NPN-Transistor [part_number=2222a package="TO92 [THT]"]
  Q5 = NPN-Transistor [part_number=2222a package="TO92 [THT]"]
  Q6 = NPN-Transistor [part_number=2222a package="TO92 [THT]"]
  LED1 = LED - 5mm [color="Green (555nm)" current=20mA package="5 mm [THT]"]
  LED2 = LED - 5mm [color="Green (555nm)" current=20mA package="5 mm [THT]"]
  LED3 = LED - 5mm [color="Green (555nm)" current=20mA package="5 mm [THT]"]
  LED4 = LED - 5mm [color="Green (555nm)" current=20mA package="5 mm [THT]"]
  LED5 = LED - 5mm [color="Green (555nm)" current=20mA package="5 mm [THT]"]
  LED6 = LED - 5mm [color="Green (555nm)" current=20mA package="5 mm [THT]"]
  LED7 = LED - 5mm [color="Green (555nm)" current=20mA package="5 mm [THT]"]
  LED8 = LED - 5mm [color="Green (555nm)" current=20mA package="5 mm [THT]"]
  LED9 = LED - 5mm [color="Green (555nm)" current=20mA package="5 mm [THT]"]
  LED10 = LED - 5mm [color="Green (555nm)" current=20mA package="5 mm [THT]"]
  LED11 = LED - 5mm [color="Green (555nm)" current=20mA package="5 mm [THT]"]
  LED12 = LED - 5mm [color="Green (555nm)" current=20mA package="5 mm [THT]"]
  LED13 = LED - 5mm [color="Green (555nm)" current=20mA package="5 mm [THT]"]
  LED14 = LED - 5mm [color="Green (555nm)" current=20mA package="5 mm [THT]"]
  LED15 = LED - 5mm [color="Green (555nm)" current=20mA package="5 mm [THT]"]
  LED16 = LED - 5mm [color="Green (555nm)" current=20mA package="5 mm [THT]"]
  LED17 = LED - 5mm [color="Green (555nm)" current=20mA package="5 mm [THT]"]
  LED18 = LED - 5mm [color="Green (555nm)" current=20mA package="5 mm [THT]"]
  LED19 = LED - 5mm [color="Green (555nm)" current=20mA package="5 mm [THT]"]
  LED20 = LED - 5mm [color="Green (555nm)" current=20mA package="5 mm [THT]"]
  LED21 = LED - 5mm [color="Green (555nm)" current=20mA package="5 mm [THT]"]
  R7 = Resistor [tolerance=±5% resistance=100 package=THT]
  R8 = Resistor [tolerance=±5% resistance=100 package=THT]
  R9 = Resistor [tolerance=±5% resistance=100 package=THT]
  R10 = Resistor [tolerance=±5% resistance=68 package=THT]
  R11 = Resistor [tolerance=±5% resistance=68 package=THT]
  R12 = Resistor [tolerance=±5% resistance=68 package=THT]
  VCC1 = Battery block 9V
  VCC2 = Battery block 9V
  VCC3 = Battery block 9V
  VCC4 = Battery block 9V

nets:
  N1: Part1.D8, R2.Pin_0
  N2: Part1.GND, Q1.E, Q2.E, Q3.E, Q4.E, Q5.E, Q6.E, VCC1.-, VCC2.-, VCC3.-, VCC4.-
  N3: Part1.D2, R1.Pin_0
  N4: Part1.D4, R3.Pin_0
  N5: Part1.D5_PWM, R4.Pin_0
  N6: Part1.D6_PWM, R5.Pin_0
  N7: Part1.D7, R6.Pin_0
  N8: Part1.VIN, R7.Pin_1, R8.Pin_1, R9.Pin_1, R10.Pin_1, R11.Pin_1, R12.Pin_1, VCC1.+, VCC2.+, VCC3.+, VCC4.+
  N9: R1.Pin_1, Q1.B
  N10: R2.Pin_1, Q2.B
  N11: R3.Pin_1, Q3.B
  N12: R4.Pin_1, Q4.B
  N13: R5.Pin_1, Q5.B
  N14: R6.Pin_1, Q6.B
  N15: Q1.C, LED1.cathode, LED2.cathode, LED3.cathode
  N16: Q2.C, LED4.cathode, LED5.cathode, LED6.cathode, LED7.cathode
  N17: Q3.C, LED8.cathode, LED9.cathode, LED10.cathode, LED11.cathode
  N18: Q4.C, LED12.cathode, LED13.cathode, LED14.cathode
  N19: Q5.C, LED15.cathode, LED16.cathode, LED17.cathode
  N20: Q6.C, LED18.cathode, LED19.cathode, LED20.cathode, LED21.cathode
  N21: LED1.anode, LED2.anode, LED3.anode, R7.Pin_0
  N22: LED4.anode, LED5.anode, LED6.anode, LED7.anode, R12.Pin_0
  N23: LED8.anode, LED11.anode
  N24: LED9.anode, LED10.anode, R11.Pin_0
  N25: LED12.anode, LED13.anode, LED14.anode, R8.Pin_0
  N26: LED15.anode, LED16.anode, LED17.anode, R9.Pin_0
  N27: LED18.anode, LED19.anode, LED20.anode, LED21.anode, R10.Pin_0
